# Fritzing sketch vfobfo_schematic (saved by Fritzing 0.9.3b)
circuit board: 8.46667cm x 5.64444cm
breadboards: 1

parts:
  Arduino_ATmega32U4 = Arduino Micro (Rev3)
  Band = SWITCH-MOMENTARY-2 [package=tactile-pth-12mm]
  Step = SWITCH-MOMENTARY-2 [package=tactile-pth-12mm]
  R1 = Resistor [tolerance=±5% resistance=10k package=THT]
  R2 = Resistor [tolerance=±5% resistance=10k package=THT]
  VFO/BFO_switch = SWITCH-MOMENTARY-2 [package=tactile-pth-12mm]
  R3 = Resistor [tolerance=±5% resistance=10k package=THT]
  OLED = OLED Monochrome 128x64 0.96 inch [part_number=326]
  Clock_Generator = Adafruit Si5351A Clock Generator [part_number="Adafruit #2045"]
  U1 = ENCODER-QUADRATURE [package=encoder-16mm-quad]
  LED1 = LED - 5mm [color="Red (633nm)" package="5 mm [THT]"]
  R4 = Resistor [tolerance=±5% resistance=1k package=THT]

nets:
  N1: Arduino_ATmega32U4.D1/TX, Step.1, R1.Pin_1
  N2: Arduino_ATmega32U4.D0/RX, Band.1, R2.Pin_1
  GND: Arduino_ATmega32U4.GND, R1.Pin_0, R2.Pin_0, R3.Pin_0, OLED.GND, Clock_Generator.GND, U1.C, LED1.cathode
  N3: Arduino_ATmega32U4.D2/SDA, OLED.MOSI_SDA, Clock_Generator.SDA
  N4: Arduino_ATmega32U4.D3/SCL, OLED.SCLK_SCK, Clock_Generator.SCL
  N5: Arduino_ATmega32U4.D7, VFO/BFO_switch.1, R3.Pin_1
  N6: Arduino_ATmega32U4.D8_PWM/A8, U1.A
  N7: Arduino_ATmega32U4.D9_PWM/A9, U1.B
  N8: Arduino_ATmega32U4.D10_PWM/A10, R4.Pin_0
  5V: Arduino_ATmega32U4.5V, Band.2, Step.2, VFO/BFO_switch.2, OLED.VIN, Clock_Generator.VIN
  N9: LED1.anode, R4.Pin_1

notes:
  Push Button Band - (D0/RX external intterupt)
  Push Button Step - (D1/TX external interrupt)
  Push Button VFO/BFO - (D7 external interrupt)
  Encoder Pin A - D08
  Encoder Pin B - D09
  LED - D10
  B
  A
  C
  Encoder
  VFO
  BFO
  D0
  D1
  D2
  D3
  D9
  D8
  D7
  D10

custom parts:
  OLED Monochrome 128x64 0.96 inch: These displays are small, only about 1" diameter, but very readable due to the high contrast of an OLED display. This display is made of 128x64 individual white OLED pixels, each one is turned on or off by the controller chip. Because the display makes its own light, no backlight is required. This reduces the power required to run the OLED and is why the display has such high contrast; we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
  Adafruit Si5351A Clock Generator: Never hunt around for another crystal again, with the Si5351A clock generator breakout from Adafruit! This chip has a precision 25MHz crystal reference and internal PLL and dividers so it can generate just about any frequency, from <8KHz up to 150+ MHz. The Si5351A clock generator is an I2C controller clock generator. It uses the onboard precision clock to drive multiple PLL's and clock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
